// Logisim project Basic Gate.circ as structural Verilog: 1 circuit, main circuit main
module main (
  input  A,
  input  B,
  input  C,
  input  _1,
  input  _1_2,
  input  Set,
  input  Enabler,
  input  Reset
);

  wire A_q, A_qn, and_1_out, and_2_out, and_3_out, and_4_out, and_5_out, and_6_out, and_7_out, and_8_out,
       B_q, B_qn, C_q, clock_1_out, not_1_out, not_2_out, not_3_out, not_4_out, not_5_out, not_6_out,
       or_1_out, or_2_out, or_3_out, or_4_out, or_5_out, or_6_out, or_7_out, or_8_out, or_9_out, or_10_out,
       or_11_out;

  not not_1 (not_1_out, A);
  not not_2 (not_2_out, B);
  not not_3 (not_3_out, C);
  or or_1 (or_1_out, not_1_out, B, C);
  and and_1 (and_1_out, not_2_out, C);
  and and_2 (and_2_out, A, not_2_out, not_3_out);
  and and_3 (and_3_out, not_1_out, not_2_out, C);
  or or_2 (or_2_out, A, B, not_3_out);
  _7_Segment_Display u_7_segment_display_1 (
    .g(or_2_out), .f(or_4_out), .a(_1), .b(or_1_out), .e(not_1_out), .d(_1), .c(or_3_out));  // open: dp
  or or_3 (or_3_out, and_1_out, A);
  or or_4 (or_4_out, and_2_out, and_3_out);
  Clock clock_1 (.out(clock_1_out));
  T_Flip_Flop u_A (.clk(clock_1_out), .T(or_6_out), .Q(A_q), .Qn(A_qn), .preset(Set), .reset(Reset), .en(Enabler));
  T_Flip_Flop u_B (.clk(clock_1_out), .T(or_7_out), .Q(B_q), .Qn(B_qn), .preset(Set), .reset(Reset), .en(Enabler));
  T_Flip_Flop u_C (.clk(clock_1_out), .T(or_5_out), .Q(C_q), .preset(Set), .reset(Reset), .en(Enabler));  // open: Qn
  and and_4 (and_4_out, A_q, B_q);
  and and_5 (and_5_out, B_q, C_q);
  or or_5 (or_5_out, A_qn, B_qn);
  or or_6 (or_6_out, and_4_out, and_5_out);
  or or_7 (or_7_out, and_4_out, C_q);
  not not_4 (not_4_out, A_q);
  not not_5 (not_5_out, B_q);
  not not_6 (not_6_out, C_q);
  or or_8 (or_8_out, not_4_out, B_q, C_q);
  and and_6 (and_6_out, not_5_out, C_q);
  and and_7 (and_7_out, A_q, not_5_out, not_6_out);
  and and_8 (and_8_out, not_4_out, not_5_out, C_q);
  or or_9 (or_9_out, A_q, B_q, not_6_out);
  or or_10 (or_10_out, and_6_out, A_q);
  or or_11 (or_11_out, and_7_out, and_8_out);
  _7_Segment_Display u_7_segment_display_2 (
    .g(or_9_out), .f(or_11_out), .a(_1_2), .b(or_8_out), .e(not_4_out), .d(_1_2), .c(or_10_out));  // open: dp

  // Notes on the sheet:
  //   Swapnil Saha Shawon
  //   2022533642
endmodule
