// Logisim project Decoder.circ as structural Verilog: 1 circuit, main circuit main
module main (
  input  Enabler,
  input  Enabler_2,
  input  [2:0] A_B_C,
  input  Set,
  input  Reset
);

  wire A_qn, and_1_out, and_2_out, B_qn, clock_1_out, decoder_1_out0, decoder_1_out1, decoder_1_out2,
       decoder_1_out3, decoder_1_out4, decoder_1_out5, decoder_1_out6, decoder_2_out0, decoder_2_out1,
       decoder_2_out2, decoder_2_out3, decoder_2_out4, decoder_2_out5, decoder_2_out6, or_1_out, or_2_out,
       or_3_out, or_4_out, or_5_out, or_6_out, or_7_out, or_8_out, or_9_out, or_10_out, or_11_out, or_12_out,
       or_13_out, or_14_out, or_15_out;
  wire [2:0] t_ff_1_q;

  Decoder #(.select(3)) decoder_1 (
    .out0(decoder_1_out0), .out1(decoder_1_out1), .out2(decoder_1_out2), .out3(decoder_1_out3),
    .out4(decoder_1_out4), .out5(decoder_1_out5), .out6(decoder_1_out6), .sel(A_B_C), .en(Enabler_2));  // open: out7
  or or_1 (or_1_out, decoder_1_out1, decoder_1_out4, decoder_1_out5, decoder_1_out6);
  or or_2 (or_2_out, decoder_1_out0, decoder_1_out1, decoder_1_out2, decoder_1_out3);
  or or_3 (or_3_out, decoder_1_out1, decoder_1_out4);
  or or_4 (or_4_out, decoder_1_out0, decoder_1_out1, decoder_1_out2, decoder_1_out3, decoder_1_out4, decoder_1_out5, decoder_1_out6);
  or or_5 (or_5_out, decoder_1_out0, decoder_1_out1, decoder_1_out2, decoder_1_out3, decoder_1_out5, decoder_1_out6);
  or or_6 (or_6_out, decoder_1_out0, decoder_1_out2, decoder_1_out3, decoder_1_out4, decoder_1_out5, decoder_1_out6);
  Clock clock_1 (.out(clock_1_out));
  _7_Segment_Display u_7_segment_display_1 (
    .g(or_6_out), .f(or_3_out), .a(or_4_out), .b(or_5_out), .e(or_2_out), .d(or_4_out), .c(or_1_out));  // open: dp
  T_Flip_Flop A (
    .clk(clock_1_out), .T(or_7_out), .Q(t_ff_1_q[2]), .Qn(A_qn), .preset(Set), .reset(Reset), .en(Enabler));
  T_Flip_Flop B (
    .clk(clock_1_out), .T(or_8_out), .Q(t_ff_1_q[1]), .Qn(B_qn), .preset(Set), .reset(Reset), .en(Enabler));
  T_Flip_Flop t_ff_1 (
    .clk(clock_1_out), .T(or_9_out), .Q(t_ff_1_q[0]), .preset(Set), .reset(Reset), .en(Enabler));  // open: Qn
  and and_1 (and_1_out, t_ff_1_q[2], t_ff_1_q[1]);
  or or_7 (or_7_out, and_1_out, and_2_out);
  and and_2 (and_2_out, t_ff_1_q[1], t_ff_1_q[0]);
  or or_8 (or_8_out, and_1_out, t_ff_1_q[0]);
  or or_9 (or_9_out, A_qn, B_qn);
  Decoder #(.select(3)) decoder_2 (
    .out0(decoder_2_out0), .out1(decoder_2_out1), .out2(decoder_2_out2), .out3(decoder_2_out3),
    .out4(decoder_2_out4), .out5(decoder_2_out5), .out6(decoder_2_out6), .sel(t_ff_1_q), .en(Enabler));  // open: out7
  or or_10 (or_10_out, decoder_2_out1, decoder_2_out4, decoder_2_out5, decoder_2_out6);
  or or_11 (or_11_out, decoder_2_out0, decoder_2_out1, decoder_2_out2, decoder_2_out3);
  or or_12 (or_12_out, decoder_2_out1, decoder_2_out4);
  or or_13 (or_13_out, decoder_2_out0, decoder_2_out1, decoder_2_out2, decoder_2_out3, decoder_2_out4, decoder_2_out5, decoder_2_out6);
  or or_14 (or_14_out, decoder_2_out0, decoder_2_out1, decoder_2_out2, decoder_2_out3, decoder_2_out5, decoder_2_out6);
  or or_15 (or_15_out, decoder_2_out0, decoder_2_out2, decoder_2_out3, decoder_2_out4, decoder_2_out5, decoder_2_out6);
  _7_Segment_Display u_7_segment_display_2 (
    .g(or_15_out), .f(or_12_out), .a(or_13_out), .b(or_14_out), .e(or_11_out), .d(or_13_out), .c(or_10_out));  // open: dp

  // Notes on the sheet:
  //   Swapnil Saha Shawon
  //   2022533642
endmodule
