// Logisim project MUX.circ as structural Verilog: 1 circuit, main circuit main
module main (
  input  [1:0] A_B,
  input  C,
  input  _0,
  input  _1,
  input  Enabler,
  input  _0_2,
  input  _1_2,
  input  Enabler_2,
  input  Set,
  input  Reset
);

  wire A_qn, and_1_out, and_2_out, B_qn, C_q, clock_1_out, multiplexer_1_out, multiplexer_2_out,
       multiplexer_3_out, multiplexer_4_out, multiplexer_5_out, multiplexer_6_out, multiplexer_7_out,
       multiplexer_8_out, multiplexer_9_out, multiplexer_10_out, multiplexer_11_out, multiplexer_12_out,
       not_1_out, not_2_out, or_1_out, or_2_out, or_3_out;
  wire [1:0] B_q;

  not not_1 (not_1_out, C);
  Multiplexer #(.select(2)) multiplexer_1 (
    .in0(_1), .in1(_1), .in2(_1), .in3(not_1_out), .out(multiplexer_1_out), .sel(A_B), .en(Enabler));
  Multiplexer #(.select(2)) multiplexer_2 (
    .in0(_1), .in1(_1), .in2(C), .in3(not_1_out), .out(multiplexer_2_out), .sel(A_B), .en(Enabler));
  Multiplexer #(.select(2)) multiplexer_3 (
    .in0(C), .in1(_0), .in2(_1), .in3(not_1_out), .out(multiplexer_3_out), .sel(A_B), .en(Enabler));
  Multiplexer #(.select(2)) multiplexer_4 (
    .in0(_1), .in1(_1), .in2(_0), .in3(_0), .out(multiplexer_4_out), .sel(A_B), .en(Enabler));
  Multiplexer #(.select(2)) multiplexer_5 (
    .in0(C), .in1(_0), .in2(not_1_out), .in3(_0), .out(multiplexer_5_out), .sel(A_B), .en(Enabler));
  Multiplexer #(.select(2)) multiplexer_6 (
    .in0(not_1_out), .in1(_1), .in2(_1), .in3(not_1_out), .out(multiplexer_6_out), .sel(A_B), .en(Enabler));
  _7_Segment_Display u_7_segment_display_1 (
    .g(multiplexer_6_out), .f(multiplexer_5_out), .a(multiplexer_1_out), .b(multiplexer_2_out),
    .e(multiplexer_4_out), .d(multiplexer_1_out), .c(multiplexer_3_out));  // open: dp
  Clock clock_1 (.out(clock_1_out));
  T_Flip_Flop A (.clk(clock_1_out), .T(or_2_out), .Q(B_q[1]), .Qn(A_qn), .preset(Set), .reset(Reset), .en(Enabler_2));
  T_Flip_Flop B (.clk(clock_1_out), .T(or_3_out), .Q(B_q[0]), .Qn(B_qn), .preset(Set), .reset(Reset), .en(Enabler_2));
  T_Flip_Flop u_C (.clk(clock_1_out), .T(or_1_out), .Q(C_q), .preset(Set), .reset(Reset), .en(Enabler_2));  // open: Qn
  and and_1 (and_1_out, B_q[1], B_q[0]);
  and and_2 (and_2_out, B_q[0], C_q);
  or or_1 (or_1_out, A_qn, B_qn);
  or or_2 (or_2_out, and_1_out, and_2_out);
  or or_3 (or_3_out, and_1_out, C_q);
  not not_2 (not_2_out, C_q);
  Multiplexer #(.select(2)) multiplexer_7 (
    .in0(_1_2), .in1(_1_2), .in2(_1_2), .in3(not_2_out), .out(multiplexer_7_out), .sel(B_q), .en(Enabler_2));
  Multiplexer #(.select(2)) multiplexer_8 (
    .in0(_1_2), .in1(_1_2), .in2(C_q), .in3(not_2_out), .out(multiplexer_8_out), .sel(B_q), .en(Enabler_2));
  Multiplexer #(.select(2)) multiplexer_9 (
    .in0(C_q), .in1(_0_2), .in2(_1_2), .in3(not_2_out), .out(multiplexer_9_out), .sel(B_q), .en(Enabler_2));
  Multiplexer #(.select(2)) multiplexer_10 (
    .in0(_1_2), .in1(_1_2), .in2(_0_2), .in3(_0_2), .out(multiplexer_10_out), .sel(B_q), .en(Enabler_2));
  Multiplexer #(.select(2)) multiplexer_11 (
    .in0(C_q), .in1(_0_2), .in2(not_2_out), .in3(_0_2), .out(multiplexer_11_out), .sel(B_q), .en(Enabler_2));
  Multiplexer #(.select(2)) multiplexer_12 (
    .in0(not_2_out), .in1(_1_2), .in2(_1_2), .in3(not_2_out), .out(multiplexer_12_out), .sel(B_q),
    .en(Enabler_2));
  _7_Segment_Display u_7_segment_display_2 (
    .g(multiplexer_12_out), .f(multiplexer_11_out), .a(multiplexer_7_out), .b(multiplexer_8_out),
    .e(multiplexer_10_out), .d(multiplexer_7_out), .c(multiplexer_9_out));  // open: dp

  // Notes on the sheet:
  //   Swapnil Saha Shawon
  //   2022533642
endmodule
