// Logisim project Universal Gate.circ as structural Verilog: 1 circuit, main circuit main
module main (
  input  A,
  input  B,
  input  C,
  input  _1,
  input  _1_2,
  input  Set,
  input  Enabler,
  input  Reset
);

  wire A_q, A_qn, and_1_out, and_2_out, B_q, B_qn, C_q, clock_1_out, nand_1_out, nand_2_out, nand_3_out,
       nand_4_out, nand_5_out, nand_6_out, nand_7_out, nand_8_out, nand_9_out, nand_10_out, nand_11_out,
       nand_12_out, nand_13_out, nand_14_out, nand_15_out, nand_16_out, nand_17_out, nand_18_out,
       nand_19_out, nand_20_out, nand_21_out, nand_22_out, nand_23_out, nand_24_out, nand_25_out,
       nand_26_out, nand_27_out, nand_28_out, nand_29_out, nand_30_out, nand_31_out, nand_32_out,
       nand_33_out, nand_34_out, nand_35_out, nand_36_out, nand_37_out, nand_38_out, nand_39_out,
       nand_40_out, nand_41_out, nand_42_out, nand_43_out, nand_44_out, nand_45_out, nand_46_out,
       nand_47_out, nand_48_out, nand_49_out, nand_50_out, or_1_out, or_2_out, or_3_out;

  nand nand_1 (nand_1_out, A, A);
  nand nand_2 (nand_2_out, B, B);
  nand nand_3 (nand_3_out, C, C);
  nand nand_4 (nand_4_out, nand_1_out, nand_1_out);
  nand nand_5 (nand_5_out, B, B);
  nand nand_6 (nand_6_out, C, C);
  nand nand_7 (nand_7_out, nand_2_out, C);
  nand nand_8 (nand_8_out, A, A);
  nand nand_9 (nand_9_out, A, nand_2_out);
  nand nand_10 (nand_10_out, nand_1_out, nand_2_out);
  nand nand_11 (nand_11_out, A, A);
  nand nand_12 (nand_12_out, B, B);
  nand nand_13 (nand_13_out, nand_3_out, nand_3_out);
  nand nand_14 (nand_14_out, nand_4_out, nand_5_out);
  nand nand_15 (nand_15_out, nand_7_out, nand_8_out);
  nand nand_16 (nand_16_out, nand_9_out, nand_9_out);
  nand nand_17 (nand_17_out, nand_10_out, nand_10_out);
  nand nand_18 (nand_18_out, nand_11_out, nand_12_out);
  nand nand_19 (nand_19_out, nand_14_out, nand_14_out);
  nand nand_20 (nand_20_out, nand_19_out, nand_6_out);
  nand nand_21 (nand_21_out, nand_16_out, nand_3_out);
  nand nand_22 (nand_22_out, nand_21_out, nand_23_out);
  nand nand_23 (nand_23_out, nand_17_out, C);
  nand nand_24 (nand_24_out, nand_18_out, nand_18_out);
  nand nand_25 (nand_25_out, nand_24_out, nand_13_out);
  _7_Segment_Display u_7_segment_display_1 (
    .g(nand_25_out), .f(nand_22_out), .a(_1), .b(nand_20_out), .e(nand_1_out), .d(_1), .c(nand_15_out));  // open: dp
  Clock clock_1 (.out(clock_1_out));
  T_Flip_Flop u_A (.clk(clock_1_out), .T(or_2_out), .Q(A_q), .Qn(A_qn), .preset(Set), .reset(Reset), .en(Enabler));
  T_Flip_Flop u_B (.clk(clock_1_out), .T(or_3_out), .Q(B_q), .Qn(B_qn), .preset(Set), .reset(Reset), .en(Enabler));
  T_Flip_Flop u_C (.clk(clock_1_out), .T(or_1_out), .Q(C_q), .preset(Set), .reset(Reset), .en(Enabler));  // open: Qn
  and and_1 (and_1_out, A_q, B_q);
  and and_2 (and_2_out, B_q, C_q);
  or or_1 (or_1_out, A_qn, B_qn);
  or or_2 (or_2_out, and_1_out, and_2_out);
  or or_3 (or_3_out, and_1_out, C_q);
  nand nand_26 (nand_26_out, A_q, A_q);
  nand nand_27 (nand_27_out, B_q, B_q);
  nand nand_28 (nand_28_out, C_q, C_q);
  nand nand_29 (nand_29_out, nand_26_out, nand_26_out);
  nand nand_30 (nand_30_out, B_q, B_q);
  nand nand_31 (nand_31_out, C_q, C_q);
  nand nand_32 (nand_32_out, nand_27_out, C_q);
  nand nand_33 (nand_33_out, A_q, A_q);
  nand nand_34 (nand_34_out, A_q, nand_27_out);
  nand nand_35 (nand_35_out, nand_26_out, nand_27_out);
  nand nand_36 (nand_36_out, A_q, A_q);
  nand nand_37 (nand_37_out, B_q, B_q);
  nand nand_38 (nand_38_out, nand_28_out, nand_28_out);
  nand nand_39 (nand_39_out, nand_29_out, nand_30_out);
  nand nand_40 (nand_40_out, nand_32_out, nand_33_out);
  nand nand_41 (nand_41_out, nand_34_out, nand_34_out);
  nand nand_42 (nand_42_out, nand_35_out, nand_35_out);
  nand nand_43 (nand_43_out, nand_36_out, nand_37_out);
  nand nand_44 (nand_44_out, nand_39_out, nand_39_out);
  nand nand_45 (nand_45_out, nand_44_out, nand_31_out);
  nand nand_46 (nand_46_out, nand_41_out, nand_28_out);
  nand nand_47 (nand_47_out, nand_46_out, nand_48_out);
  nand nand_48 (nand_48_out, nand_42_out, C_q);
  nand nand_49 (nand_49_out, nand_43_out, nand_43_out);
  nand nand_50 (nand_50_out, nand_49_out, nand_38_out);
  _7_Segment_Display u_7_segment_display_2 (
    .g(nand_50_out), .f(nand_47_out), .a(_1_2), .b(nand_45_out), .e(nand_26_out), .d(_1_2), .c(nand_40_out));  // open: dp

  // Notes on the sheet:
  //   Swapnil Saha Shawon
  //   2022533642
endmodule
